# Fritzing sketch M01P01_PowerSupply (saved by Fritzing 0.9.3b)
breadboards: 1

parts:
  Componente1 = Solar Cell
  Componente2 = Solar Cell
  Componente3 = Solar Cell
  Componente4 = Solar Cell
  TP1 = TP4056 [chip_label=TP4056 package="DIP (Dual Inline) [THT]"]
  BAT1 = 18650 battery holder [package=battery-18650-kit]
  Componente5 = VERTER 5V USB Buck-Boost

nets:
  N1: Componente1.+, Componente2.+, Componente3.+, Componente4.+, TP1.pin1
  N2: Componente1.-, Componente2.-, Componente3.-, Componente4.-, TP1.pin2
  N3: TP1.pin3, Componente5.VIN
  N4: TP1.pin4, BAT1.+
  N5: TP1.pin5, BAT1.-
  N6: TP1.pin6, Componente5.GND

notes:
  DC-DC step-up USB voltage regulator (from 0.9-5V to 5V - 600 mA), with a USB-A (female) output.
  I didnt find this part here in Fritzing

custom parts:
  TP4056: A DIP stand-in part for whatever IC you want. With 6 pins on a 300mil dual inline package (DIP) footprint.
  18650 battery holder: 18650 Battery Holder
  VERTER 5V USB Buck-Boost: VERTER can take battery voltages from 3-12VDC and output a nice 5V DC, which makes it a perfect universal power supply for your portable project! Where Verter really shines is when you have a battery or power range that can fluctuate a lot, or you don't know what you'll end up using.
