# Fritzing sketch M01P02_NodeMCU_Sensors (saved by Fritzing 0.9.3b)
breadboards: 1

parts:
  U1 = NodeMCU V3.0
  BMP280 = BMP280 Breakout Board [part_number=BMP280]
  LDR = Photocell (LDR) [package=THT]
  4_7K = Resistor [tolerance=±5% resistance=4.7k package=THT]

nets:
  N1: U1.D1, BMP280.SCL
  N2: U1.D2, BMP280.SDA
  N3: U1.3V3, LDR.pin_1
  N4: U1.GND, 4_7K.Pin_0
  N5: U1.A0, LDR.pin_0, 4_7K.Pin_1

custom parts:
  NodeMCU V3.0: NodeMcu V3 Lua WIFI Development Board
  BMP280 Breakout Board: This is a breakout board for the Bosch Sensortec BMP280, "an absolute barometric pressure sensor especially designed for mobile applications." The operation range is 300 to 1100 hPa. Supply voltage is 1.2 to 3.6V. Operating temperature range is -40 to +85 °C.
