# Fritzing sketch M02P02_Running (saved by Fritzing 0.9.3b)
breadboards: 1

parts:
  ESP32_-_Back1 = ESP32 - CAM
  5V = Power plug

nets:
  N1: ESP32_-_Back1.GND#7, 5V.GND
  5V: ESP32_-_Back1.5V, 5V.VCC

custom parts:
  ESP32 - CAM: The ESP32-CAM has a very competitive small-size camera module that can operate independently as a minimum system with a footprint of only 27*40.5*4.5mm and a deep sleep current of up to 6mA.
